# Fritzing sketch Pi 5 Tries (saved by Fritzing 0.9.5d)
circuit board: 14.8754cm x 12.6046cm
breadboards: 1

parts:
  RASPI = Raspberry Pi 5
  GYRO = Triple Axis Gyro Breakout ITG-3200
  BAT3 = LIPO-1000mAh [package=lipo-1000]
  BAT1 = Battery Holders [package=lipo-1100mAh]
  BAT2 = LIPO-1000mAh [package=lipo-1000]
  SCREEN = Nokia 6100 Color LCD [package=nokia6100_lcd]
  CAMERA = Adafruit OV5640 Camera Breakout [part_number=#5673]
  DC1 = DC_DC_XL4016 [chip_label=XL4016 package=board_screw]  # not connected
  DC2 = DC_DC_XL4016 [chip_label=XL4016 package=board_screw]  # not connected
  REGULATOR = XL4015 DC-DC CC CV module (blue)

nets (from the schematic view):
  3V3: RASPI.3V3, SCREEN.VDIGITAL, SCREEN.VDISPLAY, SCREEN.VLED, CAMERA.3.3V
  5V: RASPI.5V, RASPI.Fan-5V, GYRO.VCC
  SDA: RASPI.GPIO2, GYRO.SDA
  SCL: RASPI.GPIO3, GYRO.SCL, CAMERA.SCL
  GND: RASPI.GND, RASPI.Fan-GND, GYRO.GND, SCREEN.GND, SCREEN.LEDGND, CAMERA.GND, REGULATOR.pin_4
  EXT_SCLK: RASPI.GPIO4, CAMERA.EXT_XCLK
  DATA2: RASPI.GPIO14, CAMERA.DATA2
  DATA3: RASPI.GPIO15, CAMERA.DATA3
  VSYNC: RASPI.GPIO17, CAMERA.VSYNC
  DATA4: RASPI.GPIO18, CAMERA.DATA4
  HSYNC: RASPI.GPIO27, CAMERA.HSYNC
  PCLK: RASPI.GPIO22, CAMERA.PCLK
  DATA5: RASPI.GPIO23, CAMERA.DATA5
  DATA6: RASPI.GPIO24, CAMERA.DATA6
  SCK: RASPI.GPIO10, SCREEN.SCK
  DIO: RASPI.GPIO9, SCREEN.DIO
  DATA7: RASPI.GPIO25, CAMERA.DATA7
  CS: RASPI.GPIO11, SCREEN.CS
  DATA8: RASPI.GPIO8, CAMERA.DATA8
  DATA9: RASPI.GPIO7, CAMERA.DATA9
  N1: RASPI.GPIO5, SCREEN.RESET
  N2: RASPI.GPIO16, GYRO.VLOGIC, GYRO.CLKIN
  N3: RASPI.GPIO20, GYRO.INT
  N4: RASPI.BAT+, REGULATOR.pin_3
  N5: BAT3.+, BAT2.-
  N6: BAT3.-, REGULATOR.pin_2
  N7: BAT1.+, REGULATOR.pin_1
  N8: BAT1.-, BAT2.+

custom parts:
  Raspberry Pi 5: The RPi5, a faster version of the awesome Raspberry Pi4B ARM Board with 40 pin gpio.
  Adafruit OV5640 Camera Breakout: Hobby-level microcontrollers are finally getting big and powerful enough to start handling camera modules that historically would have required a full computer or FPGA to handle. The RP2040 and ESP32-Sx series of chips, for example, have enough pins to communicate with the 8-bit data output, DMA to quickly grab a frame, and the necessary RAM to buffer a raw snapshot. Now all we need is a nice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
  DC_DC_XL4016: DC-DC Converter step down voltage regulator XL4016 custom sketch.
  XL4015 DC-DC CC CV module (blue): XL4015 DC-DC CC/CV module blue
